// Logisim project Design.circ as structural Verilog: 5 circuits, main circuit Processor
module Processor (
  output [19:0] Result,
  output [4:0] RD_IMM,
  output [4:0] RT,
  output [4:0] RS,
  output [4:0] OP,
  output [1:0] ALUop
);

  wire alu_1_beq, CLK_out, control_unit_1_alusrc, control_unit_1_jump, control_unit_1_r_d,
       control_unit_1_r_w, Reset_out;
  wire [4:0] multiplexer_3_out;
  wire [4:1] rom_1_data;
  wire [19:0] adder_1_out, adder_2_out, bit_extender_1_out, multiplexer_1_out, multiplexer_2_out,
       multiplexer_4_out, PC_q, register_1_register1_data, register_1_register2_data;

  Control_Unit control_unit_1 (
    .in_1({1'b0, OP[3:0]}), .R_W(control_unit_1_r_w), .R_D(control_unit_1_r_d),
    .ALUsrc(control_unit_1_alusrc), .Jump(control_unit_1_jump), .ALUop(ALUop));
  Adder #(.width(20)) adder_1 (.a(PC_q), .b(20'h4), .out(adder_1_out));  // open: cin, cout
  Multiplexer #(.width(20)) multiplexer_1 (
    .in0(adder_2_out), .in1(adder_1_out), .out(multiplexer_1_out), .sel(alu_1_beq));  // open: en
  Multiplexer #(.width(20)) multiplexer_2 (
    .in0(multiplexer_1_out), .in1(20'h5), .out(multiplexer_2_out), .sel(control_unit_1_jump));  // open: en
  Button Reset (.out(Reset_out));
  Register_part #(.width(20)) PC (.D(multiplexer_2_out), .Q(PC_q), .clk(CLK_out), .clr(Reset_out));  // open: en
  Clock CLK (.out(CLK_out));
  Adder #(.width(20)) adder_2 (.a(PC_q), .b(20'h1), .out(adder_2_out));  // open: cin, cout
  ROM #(.addrWidth(20), .dataWidth(20)) rom_1 (
    .addr(PC_q), .data({rom_1_data, OP[3:0], RS[3:0], RT[3:0], RD_IMM[3:0]}));  // open: sel
  assign bit_extender_1_out = {{15{1'b0}}, {1'b0, RD_IMM[3:0]}};  // Bit_Extender bit_extender_1
  Multiplexer #(.width(5)) multiplexer_3 (
    .in0({1'b0, RD_IMM[3:0]}), .in1({1'b0, RT[3:0]}), .out(multiplexer_3_out), .sel(control_unit_1_r_d));  // open: en
  Register register_1 (
    .Data(Result), .Register1_Data(register_1_register1_data), .Register2_Data(register_1_register2_data),
    .Write_register(multiplexer_3_out), .Write_register_2(control_unit_1_r_w),
    .Read_Register1({1'b0, RS[3:0]}), .Read_Register2({1'b0, RT[3:0]}), .Clock(CLK_out));
  Multiplexer #(.width(20)) multiplexer_4 (
    .in0(register_1_register2_data), .in1(bit_extender_1_out), .out(multiplexer_4_out),
    .sel(control_unit_1_alusrc));  // open: en
  ALU alu_1 (
    .A(register_1_register1_data), .B(multiplexer_4_out), .R(Result), .Beq(alu_1_beq), .ALUop(ALUop));  // open: Cout, Cin

  assign OP[4] = 1'b0;
  assign RD_IMM[4] = 1'b0;
  assign RS[4] = 1'b0;
  assign RT[4] = 1'b0;

  // Notes on the sheet:
  //   Control Unit
  //   contents of rom_1 (hex, n*v repeats v):
  //   1012 1023 1030 1040 4000 2320 414 1331 3000 1450
endmodule

module ALU_1_Bit (
  input  A,
  input  B,
  input  Cin,
  input  [1:0] ALUop,
  output R,
  output Cout
);

  wire adder_1_out, comparator_1_eq;

  Adder #(.width(1)) adder_1 (.a(A), .b(B), .out(adder_1_out), .cin(Cin), .cout(Cout));
  Comparator #(.width(1)) comparator_1 (.a(A), .b(B), .eq(comparator_1_eq));  // open: gt, lt
  Multiplexer #(.select(2)) multiplexer_1 (
    .in0(adder_1_out), .in1(comparator_1_eq), .out(R), .sel(ALUop));  // open: in2, in3, en
endmodule

module ALU (
  input  Cin,
  input  [19:0] A,
  input  [19:0] B,
  input  [1:0] ALUop,
  output [19:0] R,
  output Beq,
  output Cout
);

  wire alu_1_bit_1_cout, alu_1_bit_2_cout, alu_1_bit_3_cout, alu_1_bit_4_cout, alu_1_bit_5_cout,
       alu_1_bit_6_cout, alu_1_bit_7_cout, alu_1_bit_8_cout, alu_1_bit_9_cout, alu_1_bit_10_cout,
       alu_1_bit_11_cout, alu_1_bit_12_cout, alu_1_bit_13_cout, alu_1_bit_14_cout, alu_1_bit_15_cout,
       alu_1_bit_16_cout, alu_1_bit_17_cout, alu_1_bit_18_cout, alu_1_bit_19_cout;

  ALU_1_Bit alu_1_bit_1 (.A(A[0]), .B(B[0]), .R(R[0]), .ALUop(ALUop), .Cin(Cin), .Cout(alu_1_bit_1_cout));
  ALU_1_Bit alu_1_bit_2 (.A(A[1]), .B(B[1]), .R(R[1]), .ALUop(ALUop), .Cin(alu_1_bit_1_cout), .Cout(alu_1_bit_2_cout));
  ALU_1_Bit alu_1_bit_3 (.A(A[2]), .B(B[2]), .R(R[2]), .ALUop(ALUop), .Cin(alu_1_bit_2_cout), .Cout(alu_1_bit_3_cout));
  ALU_1_Bit alu_1_bit_4 (.A(A[3]), .B(B[3]), .R(R[3]), .ALUop(ALUop), .Cin(alu_1_bit_3_cout), .Cout(alu_1_bit_4_cout));
  ALU_1_Bit alu_1_bit_5 (.A(A[4]), .B(B[4]), .R(R[4]), .ALUop(ALUop), .Cin(alu_1_bit_4_cout), .Cout(alu_1_bit_5_cout));
  ALU_1_Bit alu_1_bit_6 (.A(A[5]), .B(B[5]), .R(R[5]), .ALUop(ALUop), .Cin(alu_1_bit_5_cout), .Cout(alu_1_bit_6_cout));
  ALU_1_Bit alu_1_bit_7 (.A(A[6]), .B(B[6]), .R(R[6]), .ALUop(ALUop), .Cin(alu_1_bit_6_cout), .Cout(alu_1_bit_7_cout));
  ALU_1_Bit alu_1_bit_8 (.A(A[7]), .B(B[7]), .R(R[7]), .ALUop(ALUop), .Cin(alu_1_bit_7_cout), .Cout(alu_1_bit_8_cout));
  ALU_1_Bit alu_1_bit_9 (.A(A[8]), .B(B[8]), .R(R[8]), .ALUop(ALUop), .Cin(alu_1_bit_8_cout), .Cout(alu_1_bit_9_cout));
  ALU_1_Bit alu_1_bit_10 (
    .A(A[9]), .B(B[9]), .R(R[9]), .ALUop(ALUop), .Cin(alu_1_bit_9_cout), .Cout(alu_1_bit_10_cout));
  ALU_1_Bit alu_1_bit_11 (
    .A(A[10]), .B(B[10]), .R(R[10]), .ALUop(ALUop), .Cin(alu_1_bit_10_cout), .Cout(alu_1_bit_11_cout));
  ALU_1_Bit alu_1_bit_12 (
    .A(A[11]), .B(B[11]), .R(R[11]), .ALUop(ALUop), .Cin(alu_1_bit_11_cout), .Cout(alu_1_bit_12_cout));
  ALU_1_Bit alu_1_bit_13 (
    .A(A[12]), .B(B[12]), .R(R[12]), .ALUop(ALUop), .Cin(alu_1_bit_12_cout), .Cout(alu_1_bit_13_cout));
  ALU_1_Bit alu_1_bit_14 (
    .A(A[13]), .B(B[13]), .R(R[13]), .ALUop(ALUop), .Cin(alu_1_bit_13_cout), .Cout(alu_1_bit_14_cout));
  ALU_1_Bit alu_1_bit_15 (
    .A(A[14]), .B(B[14]), .R(R[14]), .ALUop(ALUop), .Cin(alu_1_bit_14_cout), .Cout(alu_1_bit_15_cout));
  ALU_1_Bit alu_1_bit_16 (
    .A(A[15]), .B(B[15]), .R(R[15]), .ALUop(ALUop), .Cin(alu_1_bit_15_cout), .Cout(alu_1_bit_16_cout));
  ALU_1_Bit alu_1_bit_17 (
    .A(A[16]), .B(B[16]), .R(R[16]), .ALUop(ALUop), .Cin(alu_1_bit_16_cout), .Cout(alu_1_bit_17_cout));
  ALU_1_Bit alu_1_bit_18 (
    .A(A[17]), .B(B[17]), .R(R[17]), .ALUop(ALUop), .Cin(alu_1_bit_17_cout), .Cout(alu_1_bit_18_cout));
  ALU_1_Bit alu_1_bit_19 (
    .A(A[18]), .B(B[18]), .R(R[18]), .ALUop(ALUop), .Cin(alu_1_bit_18_cout), .Cout(alu_1_bit_19_cout));
  ALU_1_Bit alu_1_bit_20 (.A(A[19]), .B(B[19]), .R(R[19]), .ALUop(ALUop), .Cin(alu_1_bit_19_cout), .Cout(Cout));
  and and_1 (Beq, R[0], R[1], R[2], R[3], R[4], R[5], R[6], R[7], R[8], R[9], R[10], R[11], R[12], R[13], R[14], R[15], R[16], R[17], R[18], R[19]);
endmodule

module Control_Unit (
  input  [4:0] in_1,
  output R_W,
  output R_D,
  output ALUsrc,
  output Jump,
  output [1:0] ALUop
);

  wire and_1_out, and_2_out, and_3_out, and_4_out, and_5_out, and_6_out, and_7_out, and_8_out, and_9_out,
       and_10_out, and_11_out, and_12_out, and_13_out, and_14_out, and_15_out, and_16_out, and_17_out,
       and_18_out, not_1_out, not_2_out, not_3_out, not_4_out, not_5_out, not_6_out, not_7_out, not_8_out,
       not_9_out, not_10_out, not_11_out, not_12_out, not_13_out, not_14_out, not_15_out, not_16_out,
       not_17_out, not_18_out, not_19_out, not_20_out, not_21_out, not_22_out, not_23_out, not_24_out,
       not_25_out, not_26_out, not_27_out, not_28_out, not_29_out;

  not not_1 (not_1_out, in_1[0]);
  not not_2 (not_2_out, in_1[1]);
  not not_3 (not_3_out, in_1[2]);
  not not_4 (not_4_out, in_1[3]);
  not not_5 (not_5_out, in_1[4]);
  not not_6 (not_6_out, in_1[3]);
  not not_7 (not_7_out, in_1[4]);
  not not_8 (not_8_out, in_1[2]);
  not not_9 (not_9_out, in_1[1]);
  not not_10 (not_10_out, in_1[2]);
  not not_11 (not_11_out, in_1[3]);
  not not_12 (not_12_out, in_1[4]);
  and and_1 (and_1_out, not_1_out, not_2_out, not_3_out, not_4_out, not_5_out);
  and and_2 (and_2_out, in_1[0], not_2_out, not_3_out, not_4_out, not_5_out);
  and and_3 (and_3_out, in_1[0], in_1[1], in_1[2], not_6_out, in_1[4]);
  and and_4 (and_4_out, in_1[0], in_1[1], in_1[2], not_6_out, not_7_out);
  and and_5 (and_5_out, in_1[0], in_1[1], not_8_out, in_1[3], in_1[4]);
  and and_6 (and_6_out, in_1[0], in_1[1], in_1[2], in_1[3], in_1[4]);
  and and_7 (and_7_out, in_1[0], not_9_out, not_10_out, not_11_out, not_12_out);
  not not_13 (not_13_out, in_1[3]);
  and and_8 (and_8_out, in_1[0], in_1[1], in_1[2], not_13_out, in_1[4]);
  not not_14 (not_14_out, in_1[3]);
  not not_15 (not_15_out, in_1[4]);
  not not_16 (not_16_out, in_1[2]);
  not not_17 (not_17_out, in_1[2]);
  not not_18 (not_18_out, in_1[3]);
  not not_19 (not_19_out, in_1[4]);
  not not_20 (not_20_out, in_1[0]);
  not not_21 (not_21_out, in_1[0]);
  and and_9 (and_9_out, in_1[0], in_1[1], in_1[2], not_14_out, not_15_out);
  and and_10 (and_10_out, in_1[0], in_1[1], in_1[2], in_1[3], in_1[4]);
  and and_11 (and_11_out, not_21_out, in_1[1], in_1[2], in_1[3], in_1[4]);
  and and_12 (and_12_out, in_1[0], in_1[1], not_16_out, in_1[3], in_1[4]);
  and and_13 (and_13_out, in_1[0], in_1[1], not_17_out, not_18_out, not_19_out);
  not not_22 (not_22_out, in_1[0]);
  not not_23 (not_23_out, in_1[2]);
  not not_24 (not_24_out, in_1[3]);
  not not_25 (not_25_out, in_1[4]);
  not not_26 (not_26_out, in_1[0]);
  not not_27 (not_27_out, in_1[1]);
  not not_28 (not_28_out, in_1[1]);
  and and_14 (and_14_out, not_20_out, in_1[1], in_1[2], in_1[3], in_1[4]);
  and and_15 (and_15_out, not_22_out, in_1[1], not_23_out, not_24_out, not_25_out);
  and and_16 (and_16_out, not_26_out, not_27_out, in_1[2], in_1[3], in_1[4]);
  not not_29 (not_29_out, in_1[2]);
  and and_17 (and_17_out, in_1[0], not_28_out, in_1[2], in_1[3], in_1[4]);
  and and_18 (and_18_out, in_1[0], in_1[1], not_29_out, in_1[3], in_1[4]);
  or or_1 (R_W, and_1_out, and_2_out, and_3_out, and_4_out, and_5_out);
  or or_2 (ALUsrc, and_6_out, and_7_out, and_8_out, and_9_out, and_12_out);
  or or_3 (Jump, and_6_out, and_14_out, and_8_out, and_13_out, and_12_out);
  or _00 (ALUop[0], and_10_out, and_11_out, and_15_out, and_16_out, and_18_out);
  or _01 (ALUop[1], and_10_out, and_11_out, and_17_out, and_16_out, and_18_out);

  assign R_D = ALUsrc;
endmodule

module Register (
  input  [4:0] Write_register,
  input  [19:0] Data,
  input  Write_register_2,
  input  [4:0] Read_Register1,
  input  Clock,
  input  [4:0] Read_Register2,
  output [19:0] Register1_Data,
  output [19:0] Register2_Data
);

  wire decoder_1_out0, decoder_1_out1, decoder_1_out2, decoder_1_out3, decoder_1_out4, decoder_1_out5,
       Reset_out;
  wire [19:0] multiplexer_1_out, s0_q, s1_q, s2_q, t0_q, t1_q, Zero_q;

  Decoder #(.select(5)) decoder_1 (
    .out0(decoder_1_out0), .out1(decoder_1_out1), .out2(decoder_1_out2), .out3(decoder_1_out3),
    .out4(decoder_1_out4), .out5(decoder_1_out5), .sel(Write_register));  // open: out6, out7, out8, out9, out10, out11, out12, out13, out14, out15, out16, out17, out18, out19, out20, out21, out22, out23, out24, out25, out26, out27, out28, out29, out30, out31, en
  Multiplexer #(.width(20)) multiplexer_1 (
    .in1(Data), .out(multiplexer_1_out), .sel(Write_register_2));  // open: in0, en
  Register_part #(.width(20)) Zero (
    .D(multiplexer_1_out), .en(decoder_1_out0), .Q(Zero_q), .clk(Clock), .clr(Reset_out));
  Register_part #(.width(20)) t0 (.D(multiplexer_1_out), .en(decoder_1_out1), .Q(t0_q), .clk(Clock), .clr(Reset_out));
  Register_part #(.width(20)) t1 (.D(multiplexer_1_out), .en(decoder_1_out2), .Q(t1_q), .clk(Clock), .clr(Reset_out));
  Register_part #(.width(20)) s0 (.D(multiplexer_1_out), .en(decoder_1_out3), .Q(s0_q), .clk(Clock), .clr(Reset_out));
  Register_part #(.width(20)) s1 (.D(multiplexer_1_out), .en(decoder_1_out4), .Q(s1_q), .clk(Clock), .clr(Reset_out));
  Register_part #(.width(20)) s2 (.D(multiplexer_1_out), .en(decoder_1_out5), .Q(s2_q), .clk(Clock), .clr(Reset_out));
  Button Reset (.out(Reset_out));
  Multiplexer #(.select(5), .width(20)) multiplexer_2 (
    .in0(Zero_q), .in1(t0_q), .in2(t1_q), .in3(s0_q), .in4(s1_q), .in5(s2_q), .out(Register1_Data),
    .sel(Read_Register1));  // open: in6, in7, in8, in9, in10, in11, in12, in13, in14, in15, in16, in17, in18, in19, in20, in21, in22, in23, in24, in25, in26, in27, in28, in29, in30, in31, en
  Multiplexer #(.select(5), .width(20)) multiplexer_3 (
    .in0(Zero_q), .in1(t0_q), .in2(t1_q), .in3(s0_q), .in4(s1_q), .in5(s2_q), .out(Register2_Data),
    .sel(Read_Register2));  // open: in6, in7, in8, in9, in10, in11, in12, in13, in14, in15, in16, in17, in18, in19, in20, in21, in22, in23, in24, in25, in26, in27, in28, in29, in30, in31, en
endmodule
